// Logisim project custom_reg.circ as structural Verilog: 12 circuits, main circuit 1bit_reg
module _1bit_reg (
  input  Clock,
  input  Data,
  input  Load,
  input  Clear,
  output Data_out
);

  wire and_1_out, and_2_out, not_1_out, not_2_out;

  and and_1 (and_1_out, Data, Load);
  not not_1 (not_1_out, Data);
  and and_2 (and_2_out, not_1_out, Load);
  not not_2 (not_2_out, Clear);
  J_K_Flip_Flop j_k_ff_1 (
    .J(and_1_out), .clk(Clock), .K(and_2_out), .Q(Data_out), .preset(1'b0), .en(not_2_out), .reset(Clear));  // open: Qn
endmodule

module Register (
  input  Clock,
  input  [31:0] Date_In,
  input  Load,
  output [31:0] Data_Out
);

  Register_part #(.width(32)) register_1 (.D(Date_In), .en(Load), .Q(Data_Out), .clk(Clock), .clr(1'b0));
endmodule

module BusRegister (
  input  Clock,
  input  [31:0] Date_In,
  input  Load,
  input  Bus,
  output [31:0] Data_Out,
  output [31:0] Bus_Out
);

  Register_part #(.width(32)) register_1 (.D(Date_In), .en(Load), .Q(Data_Out), .clk(Clock), .clr(1'b0));
  assign Bus_Out = Bus ? Data_Out : 32'bz;  // Controlled_Buffer controlled_buffer_1
endmodule

module ClearRegister (
  input  Clock,
  input  [31:0] Date_In,
  input  Load,
  input  Clear,
  input  Bus,
  output [31:0] Data_Out,
  output [31:0] Bus_Out
);

  Register_part #(.width(32)) register_1 (.D(Date_In), .en(Load), .Q(Data_Out), .clk(Clock), .clr(Clear));
  assign Bus_Out = Bus ? Data_Out : 32'bz;  // Controlled_Buffer controlled_buffer_1
endmodule

module CountRegister (
  input  Clock,
  input  [31:0] Date_In,
  input  Count,
  input  Load,
  input  Bus,
  output [31:0] Data_Out,
  output [31:0] Bus_Out
);

  wire or_1_out;
  wire [31:0] adder_1_out, multiplexer_1_out;

  Adder #(.width(32)) adder_1 (.a(Data_Out), .b({32{1'b0}}), .out(adder_1_out), .cin(1'b1));  // open: cout
  Multiplexer #(.width(32), .enable("false")) multiplexer_1 (
    .in0(Date_In), .in1(adder_1_out), .out(multiplexer_1_out), .sel(Count));
  or or_1 (or_1_out, Count, Load);
  Register_part #(.width(32)) register_1 (.D(multiplexer_1_out), .en(or_1_out), .Q(Data_Out), .clk(Clock), .clr(1'b0));
  assign Bus_Out = Bus ? Data_Out : 32'bz;  // Controlled_Buffer controlled_buffer_1
endmodule

module ACC (
  input  CLOCK,
  input  [31:0] INPUT,
  input  LOAD,
  input  CLEAR,
  input  BUS,
  output [31:0] OUTPUT,
  output [31:0] BUS_OUT
);

  ClearRegister clearregister_1 (
    .Date_In(INPUT), .Clock(CLOCK), .Load(LOAD), .Clear(CLEAR), .Bus(BUS), .Data_Out(OUTPUT),
    .Bus_Out(BUS_OUT));
endmodule

module AR (
  input  CLOCK,
  input  [31:0] INPUT,
  input  LOAD,
  output [31:0] OUTPUT
);

  Register register_1 (.Date_In(INPUT), .Clock(CLOCK), .Load(LOAD), .Data_Out(OUTPUT));
endmodule

module DR (
  input  CLOCK,
  input  [31:0] INPUT,
  input  LOAD,
  input  BUS,
  output [31:0] OUTPUT,
  output [31:0] BUS_OUT
);

  BusRegister busregister_1 (
    .Date_In(INPUT), .Clock(CLOCK), .Load(LOAD), .Bus(BUS), .Data_Out(OUTPUT), .Bus_Out(BUS_OUT));
endmodule

module IR (
  input  CLOCK,
  input  [31:0] INPUT,
  input  LOAD,
  output [31:0] OUTPUT
);

  Register register_1 (.Date_In(INPUT), .Clock(CLOCK), .Load(LOAD), .Data_Out(OUTPUT));
endmodule

module OUTR (
  input  CLOCK,
  input  [31:0] INPUT,
  input  LOAD,
  output [31:0] OUTPUT
);

  Register register_1 (.Date_In(INPUT), .Clock(CLOCK), .Load(LOAD), .Data_Out(OUTPUT));
endmodule

module PC (
  input  CLOCK,
  input  [31:0] INPUT,
  input  COUNT,
  input  LOAD,
  input  BUS,
  output [31:0] OUTPUT,
  output [31:0] BUS_OUT
);

  CountRegister countregister_1 (
    .Date_In(INPUT), .Clock(CLOCK), .Count(COUNT), .Load(LOAD), .Bus(BUS), .Data_Out(OUTPUT),
    .Bus_Out(BUS_OUT));
endmodule

module R (
  input  CLOCK,
  input  [31:0] INPUT,
  input  LOAD,
  input  BUS,
  output [31:0] OUTPUT,
  output [31:0] BUS_OUT
);

  BusRegister busregister_1 (
    .Date_In(INPUT), .Clock(CLOCK), .Load(LOAD), .Bus(BUS), .Data_Out(OUTPUT), .Bus_Out(BUS_OUT));
endmodule
