// Logisim project bin_converter.circ as structural Verilog: 2 circuits, main circuit bin_converter
module bin_converter (
  input  [2:0] Input,
  output a,
  output b,
  output c,
  output d,
  output e,
  output f,
  output g
);

  wire and_3_out, and_4_out, and_5_out;

  and and_1 (a, Input[2], Input[1], Input[0]);
  and and_2 (b, Input[2], Input[1]);
  and and_3 (and_3_out, Input[2], Input[0]);
  and and_4 (and_4_out, Input[2], Input[1]);
  and and_5 (and_5_out, Input[1], Input[0]);
  or or_1 (f, Input[1], Input[2]);
  or or_2 (g, Input[0], Input[1], Input[2]);
  or or_3 (c, and_3_out, and_4_out);
  or or_4 (e, and_5_out, Input[2]);

  assign d = Input[2];

  // Notes on the sheet:
  //   Ryan Florida
  //   OLA3
  //   binary converter
endmodule

module display (
  input  [2:0] Input
);

  wire bin_converter_1_a, bin_converter_1_b, bin_converter_1_c, bin_converter_1_d, bin_converter_1_e,
       bin_converter_1_f, bin_converter_1_g;

  bin_converter bin_converter_1 (
    .Input(Input), .a(bin_converter_1_a), .b(bin_converter_1_b), .c(bin_converter_1_c),
    .d(bin_converter_1_d), .e(bin_converter_1_e), .f(bin_converter_1_f), .g(bin_converter_1_g));
  LED led_1 (.in(bin_converter_1_a));
  LED led_2 (.in(bin_converter_1_b));
  LED led_3 (.in(bin_converter_1_c));
  LED led_4 (.in(bin_converter_1_d));
  LED led_5 (.in(bin_converter_1_e));
  LED led_6 (.in(bin_converter_1_f));
  LED led_7 (.in(bin_converter_1_g));

  // Notes on the sheet:
  //   Ryan Florida
  //   OLA3
  //   Display
  //   7
  //   6
  //   5
  //   4
  //   3
  //   2
  //   1
endmodule
