// Logisim project mod_counter.circ as structural Verilog: 2 circuits, main circuit Mod9
module Mod9 (
  input  Clock,
  output [3:0] Output
);

  wire A_qn, and_1_out, and_2_out, and_3_out, B_qn, C_qn, D_qn, or_1_out;

  and and_1 (and_1_out, Output[0], Output[1], B_qn);
  or or_1 (or_1_out, D_qn, C_qn);
  and and_2 (and_2_out, B_qn, Output[0]);
  and and_3 (and_3_out, A_qn, B_qn);
  J_K_Flip_Flop A (
    .J(and_1_out), .clk(Clock), .K(1'b1), .Q(Output[3]), .Qn(A_qn), .preset(1'b0), .en(1'b1), .reset(1'b0));
  J_K_Flip_Flop B (
    .J(or_1_out), .clk(Clock), .K(1'b1), .Q(Output[2]), .Qn(B_qn), .preset(1'b0), .en(1'b1), .reset(1'b0));
  J_K_Flip_Flop C (
    .J(and_2_out), .clk(Clock), .K(and_2_out), .Q(Output[1]), .Qn(C_qn), .preset(1'b0), .en(1'b1),
    .reset(1'b0));
  J_K_Flip_Flop D (
    .J(and_3_out), .clk(Clock), .K(B_qn), .Q(Output[0]), .Qn(D_qn), .preset(1'b0), .en(1'b1), .reset(1'b0));

  // Notes on the sheet:
  //   Ryan Florida
  //   OLA4
  //   Mod 9 Circuit
endmodule

module Display (
  input  DP
);

  wire clock_1_out, n7segdecoder_1_a, n7segdecoder_1_b, n7segdecoder_1_c, n7segdecoder_1_d,
       n7segdecoder_1_dp_out, n7segdecoder_1_e, n7segdecoder_1_f, n7segdecoder_1_g;
  wire [3:0] mod9_1_output;

  Clock clock_1 (.out(clock_1_out));
  Mod9 mod9_1 (.Clock(clock_1_out), .Output(mod9_1_output));
  _7SegDecoder u_7segdecoder_1 (
    .BCD_IN(mod9_1_output), .DP_IN(DP), .a(n7segdecoder_1_a), .b(n7segdecoder_1_b), .c(n7segdecoder_1_c),
    .d(n7segdecoder_1_d), .e(n7segdecoder_1_e), .f(n7segdecoder_1_f), .g(n7segdecoder_1_g),
    .DP_OUT(n7segdecoder_1_dp_out));
  _7_Segment_Display u_7_segment_display_1 (
    .g(n7segdecoder_1_g), .f(n7segdecoder_1_f), .a(n7segdecoder_1_a), .b(n7segdecoder_1_b),
    .e(n7segdecoder_1_e), .d(n7segdecoder_1_d), .c(n7segdecoder_1_c), .dp(n7segdecoder_1_dp_out));

  // Notes on the sheet:
  //   Ryan Florida
  //   OLA4
  //   Mod 9 Display
endmodule
