// Logisim project seven_seg.circ as structural Verilog: 3 circuits, main circuit Display
module Display (
  input  [3:0] BCD,
  input  DP
);

  wire n7segdecoder_1_a, n7segdecoder_1_b, n7segdecoder_1_c, n7segdecoder_1_d, n7segdecoder_1_dp_out,
       n7segdecoder_1_e, n7segdecoder_1_f, n7segdecoder_1_g;

  _7SegDecoder u_7segdecoder_1 (
    .BCD_IN(BCD), .DP_IN(DP), .a(n7segdecoder_1_a), .b(n7segdecoder_1_b), .c(n7segdecoder_1_c),
    .d(n7segdecoder_1_d), .e(n7segdecoder_1_e), .f(n7segdecoder_1_f), .g(n7segdecoder_1_g),
    .DP_OUT(n7segdecoder_1_dp_out));
  _7_Segment_Display u_7_segment_display_1 (
    .g(n7segdecoder_1_g), .f(n7segdecoder_1_f), .a(n7segdecoder_1_a), .b(n7segdecoder_1_b),
    .e(n7segdecoder_1_e), .d(n7segdecoder_1_d), .c(n7segdecoder_1_c), .dp(n7segdecoder_1_dp_out));

  // Notes on the sheet:
  //   Ryan Florida
  //   CLA3
  //   Display
endmodule

module _7SegDecoder (
  input  [3:0] BCD_IN,
  input  DP_IN,
  output a,
  output b,
  output c,
  output d,
  output e,
  output f,
  output g,
  output DP_OUT
);

  _7SegPLD u_7segpld_1 (
    .D(BCD_IN[3]), .C(BCD_IN[2]), .B(BCD_IN[1]), .A(BCD_IN[0]), .a_2(a), .b_2(b), .c_2(c), .d_2(d), .e(e),
    .f(f), .g(g));

  assign DP_OUT = DP_IN;

  // Notes on the sheet:
  //   Ryan Florida
  //   CLA3
  //   7 Segment Decoder
endmodule

module _7SegPLD (
  input  D,
  input  C,
  input  B,
  input  A,
  output a_2,
  output b_2,
  output c_2,
  output d_2,
  output e,
  output f,
  output g
);

  wire and_1_out, and_2_out, and_3_out, and_4_out, and_5_out, and_6_out, and_7_out, and_8_out, and_9_out,
       and_10_out, and_11_out, and_12_out, and_13_out, and_14_out, and_15_out, and_16_out, and_17_out,
       and_18_out, and_19_out, and_20_out, and_21_out, and_22_out, and_23_out, not_1_out, not_2_out,
       not_3_out, not_4_out, not_5_out, not_6_out, not_7_out, not_8_out, not_9_out, not_10_out, not_11_out,
       not_12_out, not_13_out, not_14_out, not_15_out, not_16_out, not_17_out, not_18_out, not_19_out,
       not_20_out, not_21_out, not_22_out, not_23_out, not_24_out, not_25_out, not_26_out, not_27_out,
       not_28_out, not_29_out;

  not not_1 (not_1_out, C);
  not not_2 (not_2_out, A);
  not not_3 (not_3_out, D);
  not not_4 (not_4_out, C);
  not not_5 (not_5_out, D);
  not not_6 (not_6_out, B);
  not not_7 (not_7_out, A);
  not not_8 (not_8_out, C);
  not not_9 (not_9_out, B);
  not not_10 (not_10_out, D);
  not not_11 (not_11_out, C);
  not not_12 (not_12_out, B);
  not not_13 (not_13_out, D);
  not not_14 (not_14_out, D);
  not not_15 (not_15_out, C);
  not not_16 (not_16_out, A);
  not not_17 (not_17_out, C);
  not not_18 (not_18_out, A);
  not not_19 (not_19_out, B);
  not not_20 (not_20_out, C);
  not not_21 (not_21_out, A);
  not not_22 (not_22_out, A);
  not not_23 (not_23_out, B);
  not not_24 (not_24_out, A);
  not not_25 (not_25_out, B);
  not not_26 (not_26_out, A);
  not not_27 (not_27_out, C);
  not not_28 (not_28_out, A);
  not not_29 (not_29_out, B);
  and and_1 (and_1_out, not_1_out, not_2_out);
  and and_2 (and_2_out, C, A);
  and and_3 (and_3_out, not_3_out, not_4_out);
  and and_4 (and_4_out, not_5_out, not_6_out, not_7_out);
  and and_5 (and_5_out, not_8_out, not_9_out);
  and and_6 (and_6_out, not_10_out, B, A);
  and and_7 (and_7_out, not_11_out, not_12_out);
  and and_8 (and_8_out, not_13_out, A);
  and and_9 (and_9_out, not_14_out, C);
  and and_10 (and_10_out, not_15_out, not_16_out);
  and and_11 (and_11_out, not_17_out, B);
  and and_12 (and_12_out, B, not_18_out);
  and and_13 (and_13_out, C, not_19_out, A);
  and and_14 (and_14_out, not_20_out, not_21_out);
  and and_15 (and_15_out, B, not_22_out);
  and and_16 (and_16_out, D, B);
  and and_17 (and_17_out, D, C);
  and and_18 (and_18_out, not_23_out, not_24_out);
  and and_19 (and_19_out, C, not_25_out);
  and and_20 (and_20_out, C, not_26_out);
  and and_21 (and_21_out, not_27_out, B);
  and and_22 (and_22_out, B, not_28_out);
  and and_23 (and_23_out, C, not_29_out);
  or or_1 (a_2, and_1_out, B, and_2_out, D);
  or or_2 (b_2, and_3_out, and_4_out, and_5_out, and_6_out);
  or or_3 (c_2, and_7_out, and_8_out, and_9_out);
  or or_4 (d_2, and_10_out, and_11_out, and_12_out, and_13_out, D);
  or or_5 (e, and_14_out, and_15_out, and_16_out, and_17_out);
  or or_6 (f, and_18_out, and_19_out, and_20_out, D);
  or or_7 (g, and_21_out, and_22_out, and_23_out, D);

  // Notes on the sheet:
  //   Ryan Florida
  //   CLA3
  //   7 Segment PLD
endmodule
